# Fritzing sketch IoT-tricolor-led-pbs-potentiometer (saved by Fritzing 0.9.4)
breadboards: 1

parts:
  Resistor_(Green_of_Tri-Color_LED) = Resistor [tolerance=±5% resistance=220 package="2512 [SMD]"]
  Resistor_(Blue_of_Tri-Color_LED) = Resistor [tolerance=±5% resistance=220 package="2512 [SMD]"]
  Resistor_(Red_of_Tri-Color_LED) = Resistor [tolerance=±5% resistance=220 package="2512 [SMD]"]
  Resistor_(PBS) = Resistor [tolerance=±5% resistance=220 package="2512 [SMD]"]
  Push-button_Switch_(PBS) = Pushbutton [package="[THT]"]
  Potentiometer = Trimmer Potentiometer [maximum_resistance=25kΩ package=THT]  # not connected
  Tri-Color_LED = RGB LED (com. anode, rbg) [package="5 mm [THT]"]
  Teensy_3_2 = Teensy 3.2  # not connected

nets:
  N1: Resistor_(Green_of_Tri-Color_LED).Pin_0, Tri-Color_LED.red_cathode
  N2: Resistor_(Blue_of_Tri-Color_LED).Pin_0, Tri-Color_LED.blue_cathode
  N3: Resistor_(Red_of_Tri-Color_LED).Pin_0, Tri-Color_LED.green_cathode
  N4: Resistor_(PBS).Pin_0, Push-button_Switch_(PBS).Pin_1, Push-button_Switch_(PBS).Pin_2
  N5: Resistor_(PBS).Pin_1, Tri-Color_LED.common_anode
  N6: Push-button_Switch_(PBS).Pin_3, Push-button_Switch_(PBS).Pin_4

notes:
  CST8227 - Interfacing
  Internet of Things (IoT)
  Tri-Color LED with push-button switch (PBS) in pull-down configuration and trim potentiometer (aka trim pot).
  Pins:
  3 (digital): push-button switch (PBS)
  23 (PWM): tri-colour LED, red
  20 (PWM): tri-colour LED, green
  21 (PWM): tri-colour LED, blue
  8 (analog): potentiometer
  Instructions:
  1) Build this circuit.
  2) Upload 'Standard Firmata Plus' to your Teensy; *quit* Arduino IDE and Teensy Loader.
  3) Run node-red
  Gerald.Hurdle@AlgonquinCollege.com

custom parts:
  Teensy 3.2: The Teensy is a complete USB-based microcontoller development system, in a very small footprint, capable of implementing many types of projects. All programming is done via the USB port. No special programmer is needed, only a standard micro-USB cable and a PC or Macintosh with a USB port. It has a USB keyboard/mouse/joystick emulation stack and can be programmed through Arduino IDE.
