# Fritzing sketch LEDwithPBS-Pull-Down (saved by Fritzing 0.9.8b)
breadboards: 1

parts:
  LED = LED - 5mm [color="Red (633nm)" current=0.030 package="5 mm [THT]"]
  Push-Button_Switch_(PBS) = Pushbutton [package="[THT]"]
  Resistor_(PBS) = Resistor [tolerance=±5% resistance=220 power=0.25 package=THT]
  Teensy_3_2 = Teensy 3.2  # not connected
  Resistor_(LED) = Resistor [tolerance=±5% resistance=220 power=0.25 package=THT]

nets:
  N1: LED.cathode, Resistor_(PBS).Pin_1
  N2: LED.anode, Resistor_(LED).Pin_1
  N3: Push-Button_Switch_(PBS).Pin_1, Push-Button_Switch_(PBS).Pin_2, Resistor_(PBS).Pin_0
  N4: Push-Button_Switch_(PBS).Pin_3, Push-Button_Switch_(PBS).Pin_4

notes:
  CST8227 - Interfacing
  Discrete red LED controlled by push-buton switch (PBS) in pull-down configuration.
  Gerald.Hurdle@AlgonquinCollege.com

custom parts:
  Teensy 3.2: The Teensy is a complete USB-based microcontoller development system, in a very small footprint, capable of implementing many types of projects. All programming is done via the USB port. No special programmer is needed, only a standard micro-USB cable and a PC or Macintosh with a USB port. It has a USB keyboard/mouse/joystick emulation stack and can be programmed through Arduino IDE.
