# Fritzing sketch LEDwithPBS-Pull-Up-Internal (saved by Fritzing 0.9.4)
breadboards: 1

parts:
  LED = LED - 5mm [color="Red (633nm)" package="5 mm [THT]"]
  Resistor_(LED) = Resistor [tolerance=±5% resistance=220 package=THT]
  Push-Button_Switch_(PBS) = Pushbutton [package="[THT]"]
  Teensy_3_2 = Teensy 3.2  # not connected

nets:
  N1: LED.cathode, Push-Button_Switch_(PBS).Pin_1, Push-Button_Switch_(PBS).Pin_2
  N2: LED.anode, Resistor_(LED).Pin_1
  N3: Push-Button_Switch_(PBS).Pin_3, Push-Button_Switch_(PBS).Pin_4

notes:
  CST8227 - Interfacing
  Discrete red LED controlled by push-buton switch (PBS) in internal pull-up configuration.
  Notice: no resistor, and no connection wire to Vcc
  Gerald.Hurdle@AlgonquinCollege.com

custom parts:
  Teensy 3.2: The Teensy is a complete USB-based microcontoller development system, in a very small footprint, capable of implementing many types of projects. All programming is done via the USB port. No special programmer is needed, only a standard micro-USB cable and a PC or Macintosh with a USB port. It has a USB keyboard/mouse/joystick emulation stack and can be programmed through Arduino IDE.
