# Fritzing sketch tricolorLEDProtoBoardLayout2 (saved by Fritzing 0.9.3b)
breadboards: 1

parts:
  Tri-Colour_LED = RGB LED (com. cathode, rgb) [package="5 mm [THT]"]
  Resistor_(Green) = Resistor [tolerance=±5% resistance=220 package="2512 [SMD]"]
  Resistor_(Blue) = Resistor [tolerance=±5% resistance=220 package="2512 [SMD]"]
  Resistor_(Red) = Resistor [tolerance=±5% resistance=220 package="2512 [SMD]"]
  Teensy_3_2 = Teensy 3.2  # not connected

nets:
  N1: Tri-Colour_LED.red_anode, Resistor_(Green).Pin_0
  N2: Tri-Colour_LED.green_anode, Resistor_(Blue).Pin_0
  N3: Tri-Colour_LED.blue_anode, Resistor_(Red).Pin_0

notes:
  CST8227 - Interfacing
  Lab 03 - PWM
  Tri-colour LED: Red, Green, Blue (RGB)
  Notes:
  * use PWM pins on the Teensy
  * this circuit is for Demos #1 and #2; you'll need to add a push-button switch (PBS) for Demos #3 and #4.
  pharasb@AlgonquinCollege.com

custom parts:
  Teensy 3.2: The Teensy is a complete USB-based microcontoller development system, in a very small footprint, capable of implementing many types of projects. All programming is done via the USB port. No special programmer is needed, only a standard micro-USB cable and a PC or Macintosh with a USB port. It has a USB keyboard/mouse/joystick emulation stack and can be programmed through Arduino IDE.
