# Fritzing sketch Lab4_Fritzing (saved by Fritzing 0.9.3b)
breadboards: 1

parts:
  Teensy_3_1 = Teensy 3.2  # not connected
  S1 = Pushbutton [package="[THT]"]
  LED1 = RGB LED (com. cathode, rgb) [package="5 mm [THT]"]
  R1 = Resistor [tolerance=±5% resistance=220 package="2010 [SMD]"]
  R2 = Resistor [tolerance=±5% resistance=220 package="2010 [SMD]"]
  R3 = Resistor [tolerance=±5% resistance=220 package="2010 [SMD]"]
  10k_resistor = Resistor [tolerance=±5% resistance=10k package=THT]
  S2 = Pushbutton [package="[THT]"]

nets:
  N1: S1.Pin_1, S1.Pin_2, LED1.common_cathode, S2.Pin_1, S2.Pin_2
  N2: S1.Pin_3, S1.Pin_4, 10k_resistor.Pin_1
  N3: LED1.red_anode, R1.Pin_0
  N4: LED1.green_anode, R2.Pin_0
  N5: LED1.blue_anode, R3.Pin_0
  N6: S2.Pin_3, S2.Pin_4

notes:
  CST8227 – Interfacing
  Lab 04 – Pushbuttons to Control LED Colors
  Control a tri-color RGB with two switches and a pull-up resistor.
  @author Hoang Do (040961749)

custom parts:
  Teensy 3.2: The Teensy is a complete USB-based microcontoller development system, in a very small footprint, capable of implementing many types of projects. All programming is done via the USB port. No special programmer is needed, only a standard micro-USB cable and a PC or Macintosh with a USB port. It has a USB keyboard/mouse/joystick emulation stack and can be programmed through Arduino IDE.
