# Fritzing sketch Blink_Segment_A (saved by Fritzing 0.9.4)
breadboards: 1

parts:
  220_Ohm_(QA) = Resistor [tolerance=±5% resistance=220 package="2512 [SMD]"]
  220_Ohm_(QC) = Resistor [tolerance=±5% resistance=220 package="2512 [SMD]"]  # not connected
  220_Ohm_(QB) = Resistor [tolerance=±5% resistance=220 package="2512 [SMD]"]  # not connected
  Shift_Register = 74HC595 [package="DIP16 [THT]"]
  220_Ohm_(QD) = Resistor [tolerance=±5% resistance=220 package="2512 [SMD]"]  # not connected
  220_Ohm_(QE) = Resistor [tolerance=±5% resistance=220 package="2512 [SMD]"]  # not connected
  220_Ohm_(QF) = Resistor [tolerance=±5% resistance=220 package="2512 [SMD]"]  # not connected
  220_Ohm_(QG) = Resistor [tolerance=±5% resistance=220 package="2512 [SMD]"]  # not connected
  220_Ohm_(QH) = Resistor [tolerance=±5% resistance=220 package="2512 [SMD]"]  # not connected
  7_Segment_Display_(Segment_A) = 7 Segment Display
  Teensy_3_2 = Teensy 3.2  # not connected

nets:
  N1: 220_Ohm_(QA).Pin_0, Shift_Register.Q0
  N2: 220_Ohm_(QA).Pin_1, 7_Segment_Display_(Segment_A).Segment_A
  N3: Shift_Register.GND, Shift_Register.OE
  N4: Shift_Register.MR, Shift_Register.VCC, 7_Segment_Display_(Segment_A).common_anode

notes:
  CST8227 - Interfacing
  Use 1 x shift register to blink segment A of 7-segment display.
  SR - Wire - Segment on 7-Segment Display
  ----------------------------------------------------------
  Q0 - blue - Segment A
  Gerald.Hurdle@AlgonquinCollege.com

custom parts:
  7 Segment Display: 7 Segment Display with common anode.
  Teensy 3.2: The Teensy is a complete USB-based microcontoller development system, in a very small footprint, capable of implementing many types of projects. All programming is done via the USB port. No special programmer is needed, only a standard micro-USB cable and a PC or Macintosh with a USB port. It has a USB keyboard/mouse/joystick emulation stack and can be programmed through Arduino IDE.
