# Fritzing sketch ShiftRegister (saved by Fritzing 0.9.4)
breadboards: 1

parts:
  Shift_Register_(TI) = 74HC595 [package="DIP16 [THT]"]
  Teensy_3_2 = Teensy 3.2  # not connected

nets:
  N1: Shift_Register_(TI).GND, Shift_Register_(TI).OE
  N2: Shift_Register_(TI).MR, Shift_Register_(TI).VCC

custom parts:
  Teensy 3.2: The Teensy is a complete USB-based microcontoller development system, in a very small footprint, capable of implementing many types of projects. All programming is done via the USB port. No special programmer is needed, only a standard micro-USB cable and a PC or Macintosh with a USB port. It has a USB keyboard/mouse/joystick emulation stack and can be programmed through Arduino IDE.
